// Logisim project 7SegLogic.circ as structural Verilog: 1 circuit, main circuit main
module main (
);

  wire A_out, B_out, BD_out, BNC_out, BNCD_out, BND_out, C_out, CD_out, CND_out, D_out, E_out, F_out,
       NBC_out, NBND_out, NCND_out, not_1_out, not_2_out, not_3_out, not_4_out, undriven, undriven_2,
       undriven_3, undriven_4;

  and BD (BD_out, undriven_2, undriven_4);
  and NBND (NBND_out, not_2_out, not_4_out);
  or A (A_out, BD_out, NBND_out, undriven, undriven_3);
  and CD (CD_out, undriven_3, undriven_4);
  or B (B_out, CD_out, NCND_out, not_2_out);
  and NCND (NCND_out, not_3_out, not_4_out);
  and NBC (NBC_out, not_2_out, undriven_3);
  or C (C_out, undriven_2, not_3_out, undriven_4);
  and CND (CND_out, undriven_3, not_4_out);
  or D (D_out, NBC_out, CND_out, BNCD_out, undriven, NBND_out);
  and BNCD (BNCD_out, undriven_2, not_3_out, undriven_4);
  or E (E_out, NBND_out, CND_out);
  and BNC (BNC_out, undriven_2, not_3_out);
  or F (F_out, NCND_out, BNC_out, BND_out, undriven);
  and BND (BND_out, undriven_2, not_4_out);
  not not_1 (not_1_out, undriven);
  not not_2 (not_2_out, undriven_2);
  not not_3 (not_3_out, undriven_3);
  not not_4 (not_4_out, undriven_4);
endmodule
