// Logisim project 9sComplement.circ as structural Verilog: 1 circuit, main circuit main
module main (
  input  in_1,
  input  in_2,
  input  in_3,
  input  in_4
);

  wire A_out, B_out, not_1_out, not_2_out, not_3_out, not_4_out;

  and A (A_out, not_1_out, not_2_out, not_3_out);
  xor B (B_out, in_2, in_3);
  not not_1 (not_1_out, in_1);
  not not_2 (not_2_out, in_2);
  not not_3 (not_3_out, in_3);
  not not_4 (not_4_out, in_4);
endmodule
