// Logisim project mul.circ as structural Verilog: 4 circuits, main circuit main
module main (
  input  [7:0] X,
  input  in_2,
  input  R
);

  wire and_1_out, and_2_out, and_3_out, and_4_out, and_5_out, and_6_out, and_7_out, and_8_out, ciso_1_out_3,
       clk_out, csadd_1_sum, csadd_2_sum, csadd_3_sum, csadd_4_sum, csadd_5_sum, csadd_6_sum, csadd_7_sum,
       main_1_out_5, sevseg_1_aa, sevseg_1_bb, sevseg_1_cc, sevseg_1_dd, sevseg_1_ee, sevseg_1_ff,
       sevseg_1_gg, sevseg_2_aa, sevseg_2_bb, sevseg_2_cc, sevseg_2_dd, sevseg_2_ee, sevseg_2_ff,
       sevseg_2_gg, sevseg_3_aa, sevseg_3_bb, sevseg_3_cc, sevseg_3_dd, sevseg_3_ee, sevseg_3_ff,
       sevseg_3_gg, sevseg_4_aa, sevseg_4_bb, sevseg_4_cc, sevseg_4_dd, sevseg_4_ee, sevseg_4_ff, sevseg_4_gg;
  wire [15:0] sipo_1_product;

  Clock clk (.out(clk_out));
  ciso ciso_1 (.SI(in_2), .CLK(clk_out), .out_3(ciso_1_out_3));
  and and_1 (and_1_out, ciso_1_out_3, X[7]);
  theTCMP_main main_1 (.A(and_1_out), .R(R), .out_5(main_1_out_5), .in_2(clk_out));  // open: out_4
  and and_2 (and_2_out, ciso_1_out_3, X[6]);
  CSADD csadd_1 (.Y(and_2_out), .X(main_1_out_5), .R(R), .sum(csadd_1_sum), .clk(clk_out));  // open: FDHA
  and and_3 (and_3_out, ciso_1_out_3, X[5]);
  and and_4 (and_4_out, ciso_1_out_3, X[4]);
  CSADD csadd_2 (.Y(and_3_out), .X(csadd_1_sum), .R(R), .sum(csadd_2_sum), .clk(clk_out));  // open: FDHA
  and and_5 (and_5_out, ciso_1_out_3, X[3]);
  and and_6 (and_6_out, ciso_1_out_3, X[2]);
  CSADD csadd_3 (.Y(and_4_out), .X(csadd_2_sum), .R(R), .sum(csadd_3_sum), .clk(clk_out));  // open: FDHA
  and and_7 (and_7_out, ciso_1_out_3, X[1]);
  and and_8 (and_8_out, ciso_1_out_3, X[0]);
  CSADD csadd_4 (.Y(and_5_out), .X(csadd_3_sum), .R(R), .sum(csadd_4_sum), .clk(clk_out));  // open: FDHA
  CSADD csadd_5 (.Y(and_6_out), .X(csadd_4_sum), .R(R), .sum(csadd_5_sum), .clk(clk_out));  // open: FDHA
  CSADD csadd_6 (.Y(and_7_out), .X(csadd_5_sum), .R(R), .sum(csadd_6_sum), .clk(clk_out));  // open: FDHA
  CSADD csadd_7 (.Y(and_8_out), .X(csadd_6_sum), .R(R), .sum(csadd_7_sum), .clk(clk_out));  // open: FDHA
  sevseg sevseg_1 (
    .A(sipo_1_product[7]), .B(sipo_1_product[5]), .C(sipo_1_product[6]), .in_4(sipo_1_product[4]),
    .AA(sevseg_1_aa), .FF(sevseg_1_ff), .GG(sevseg_1_gg), .BB(sevseg_1_bb), .EE(sevseg_1_ee),
    .DD(sevseg_1_dd), .CC(sevseg_1_cc));
  sevseg sevseg_2 (
    .A(sipo_1_product[11]), .B(sipo_1_product[9]), .C(sipo_1_product[10]), .in_4(sipo_1_product[8]),
    .AA(sevseg_2_aa), .FF(sevseg_2_ff), .GG(sevseg_2_gg), .BB(sevseg_2_bb), .EE(sevseg_2_ee),
    .DD(sevseg_2_dd), .CC(sevseg_2_cc));
  sevseg sevseg_3 (
    .A(sipo_1_product[15]), .B(sipo_1_product[13]), .C(sipo_1_product[14]), .in_4(sipo_1_product[12]),
    .AA(sevseg_3_aa), .FF(sevseg_3_ff), .GG(sevseg_3_gg), .BB(sevseg_3_bb), .EE(sevseg_3_ee),
    .DD(sevseg_3_dd), .CC(sevseg_3_cc));
  sipo sipo_1 (.SI(csadd_7_sum), .CLK(clk_out), .product(sipo_1_product));
  sevseg sevseg_4 (
    .A(sipo_1_product[3]), .B(sipo_1_product[1]), .C(sipo_1_product[2]), .in_4(sipo_1_product[0]),
    .AA(sevseg_4_aa), .FF(sevseg_4_ff), .GG(sevseg_4_gg), .BB(sevseg_4_bb), .EE(sevseg_4_ee),
    .DD(sevseg_4_dd), .CC(sevseg_4_cc));
  _7_Segment_Display u_7_segment_display_1 (
    .g(sevseg_1_gg), .f(sevseg_1_bb), .a(sevseg_1_aa), .b(sevseg_1_ff), .e(sevseg_1_ee), .d(sevseg_1_dd),
    .c(sevseg_1_cc));  // open: dp
  _7_Segment_Display u_7_segment_display_2 (
    .g(sevseg_2_gg), .f(sevseg_2_bb), .a(sevseg_2_aa), .b(sevseg_2_ff), .e(sevseg_2_ee), .d(sevseg_2_dd),
    .c(sevseg_2_cc));  // open: dp
  _7_Segment_Display u_7_segment_display_3 (
    .g(sevseg_3_gg), .f(sevseg_3_bb), .a(sevseg_3_aa), .b(sevseg_3_ff), .e(sevseg_3_ee), .d(sevseg_3_dd),
    .c(sevseg_3_cc));  // open: dp
  _7_Segment_Display u_7_segment_display_4 (
    .g(sevseg_4_gg), .f(sevseg_4_bb), .a(sevseg_4_aa), .b(sevseg_4_ff), .e(sevseg_4_ee), .d(sevseg_4_dd),
    .c(sevseg_4_cc));  // open: dp
endmodule

module ciso (
  input  SI,
  input  CLK,
  output out_3
);

  wire d_ff_1_q, d_ff_2_q, d_ff_3_q, d_ff_4_q, d_ff_5_q, d_ff_6_q, d_ff_7_q;

  D_Flip_Flop d_ff_1 (.D(SI), .clk(CLK), .Q(d_ff_1_q));  // open: Qn, preset, reset
  D_Flip_Flop d_ff_2 (.D(d_ff_1_q), .clk(CLK), .Q(d_ff_2_q));  // open: Qn, preset, reset
  D_Flip_Flop d_ff_3 (.D(d_ff_2_q), .clk(CLK), .Q(d_ff_3_q));  // open: Qn, preset, reset
  D_Flip_Flop d_ff_4 (.D(d_ff_3_q), .clk(CLK), .Q(d_ff_4_q));  // open: Qn, preset, reset
  D_Flip_Flop d_ff_5 (.D(d_ff_4_q), .clk(CLK), .Q(d_ff_5_q));  // open: Qn, preset, reset
  D_Flip_Flop d_ff_6 (.D(d_ff_5_q), .clk(CLK), .Q(d_ff_6_q));  // open: Qn, preset, reset
  D_Flip_Flop d_ff_7 (.D(d_ff_6_q), .clk(CLK), .Q(d_ff_7_q));  // open: Qn, preset, reset
  D_Flip_Flop d_ff_8 (.D(d_ff_7_q), .clk(CLK), .Q(out_3));  // open: Qn, preset, reset
endmodule

module sipo (
  input  SI,
  input  CLK,
  output [15:0] product
);

  D_Flip_Flop d_ff_1 (.D(SI), .clk(CLK), .Q(product[15]));  // open: Qn, preset, reset
  D_Flip_Flop d_ff_2 (.D(product[15]), .clk(CLK), .Q(product[14]));  // open: Qn, preset, reset
  D_Flip_Flop d_ff_3 (.D(product[14]), .clk(CLK), .Q(product[13]));  // open: Qn, preset, reset
  D_Flip_Flop d_ff_4 (.D(product[13]), .clk(CLK), .Q(product[12]));  // open: Qn, preset, reset
  D_Flip_Flop d_ff_5 (.D(product[12]), .clk(CLK), .Q(product[11]));  // open: Qn, preset, reset
  D_Flip_Flop d_ff_6 (.D(product[11]), .clk(CLK), .Q(product[10]));  // open: Qn, preset, reset
  D_Flip_Flop d_ff_7 (.D(product[10]), .clk(CLK), .Q(product[9]));  // open: Qn, preset, reset
  D_Flip_Flop d_ff_8 (.D(product[9]), .clk(CLK), .Q(product[8]));  // open: Qn, preset, reset
  D_Flip_Flop d_ff_9 (.D(product[8]), .clk(CLK), .Q(product[7]));  // open: Qn, preset, reset
  D_Flip_Flop d_ff_10 (.D(product[7]), .clk(CLK), .Q(product[6]));  // open: Qn, preset, reset
  D_Flip_Flop d_ff_11 (.D(product[6]), .clk(CLK), .Q(product[5]));  // open: Qn, preset, reset
  D_Flip_Flop d_ff_12 (.D(product[5]), .clk(CLK), .Q(product[4]));  // open: Qn, preset, reset
  D_Flip_Flop d_ff_13 (.D(product[4]), .clk(CLK), .Q(product[3]));  // open: Qn, preset, reset
  D_Flip_Flop d_ff_14 (.D(product[3]), .clk(CLK), .Q(product[2]));  // open: Qn, preset, reset
  D_Flip_Flop d_ff_15 (.D(product[2]), .clk(CLK), .Q(product[1]));  // open: Qn, preset, reset
  D_Flip_Flop d_ff_16 (.D(product[1]), .clk(CLK), .Q(product[0]));  // open: Qn, preset, reset
endmodule

module sevseg (
  input  A,
  input  B,
  input  C,
  input  in_4,
  output AA,
  output FF,
  output GG,
  output BB,
  output EE,
  output DD,
  output CC
);

  wire and_1_out, and_2_out, and_3_out, and_4_out, and_5_out, and_6_out, and_7_out, and_8_out, and_9_out,
       not_1_out, not_2_out, not_3_out, not_4_out;

  and and_1 (and_1_out, B, in_4);
  and and_2 (and_2_out, not_2_out, not_4_out);
  or or_1 (AA, and_1_out, and_2_out, A, C);
  and and_3 (and_3_out, C, in_4);
  or or_2 (BB, and_3_out, and_4_out, not_2_out);
  and and_4 (and_4_out, not_3_out, not_4_out);
  and and_5 (and_5_out, not_2_out, C);
  or or_3 (CC, B, not_3_out, in_4);
  and and_6 (and_6_out, C, not_4_out);
  or or_4 (DD, and_5_out, and_6_out, and_7_out, A, and_2_out);
  and and_7 (and_7_out, B, not_3_out, in_4);
  or or_5 (EE, and_2_out, and_6_out);
  and and_8 (and_8_out, B, not_3_out);
  and and_9 (and_9_out, B, not_4_out);
  or or_6 (FF, and_4_out, and_8_out, and_9_out, A);
  or G (GG, and_5_out, and_6_out, and_8_out, A);
  not not_1 (not_1_out, A);
  not not_2 (not_2_out, B);
  not not_3 (not_3_out, C);
  not not_4 (not_4_out, in_4);
endmodule
